// Logisim project Projeto_FINAL.circ as structural Verilog: 4 circuits, main circuit ULA
module ULA (
  input  \DIREÇÃO ,
  input  [3:0] in_2,
  input  [3:0] in_3,
  input  [2:0] in_4,
  output [3:0] SAIDA,
  output OVERFLOW,
  output ZERO
);

  wire adder_1_cout, and_1_out, and_2_out, decoder_1_out0, decoder_1_out1, decoder_1_out2, decoder_1_out3,
       decoder_1_out4, decoder_1_out5, decoder_1_out6, decoder_1_out7, not_2_out, subtractor_1_bout;
  wire [3:0] adder_1_out, controlled_buffer_6_out, not_1_out, or_2_out, shifter_1_out, shifter_2_out,
       subtractor_1_out;

  or or_1 (OVERFLOW, and_1_out, and_2_out);
  and and_1 (and_1_out, subtractor_1_bout, decoder_1_out2);
  and and_2 (and_2_out, adder_1_cout, decoder_1_out1);
  Decoder #(.select(3)) decoder_1 (
    .out0(decoder_1_out0), .out1(decoder_1_out1), .out2(decoder_1_out2), .out3(decoder_1_out3),
    .out4(decoder_1_out4), .out5(decoder_1_out5), .out6(decoder_1_out6), .out7(decoder_1_out7), .sel(in_4));  // open: en
  assign SAIDA = decoder_1_out0 ? in_3 : 4'bz;  // Controlled_Buffer controlled_buffer_1
  Adder #(.width(4)) adder_1 (.a(in_2), .b(in_3), .out(adder_1_out), .cout(adder_1_cout));  // open: cin
  assign SAIDA = decoder_1_out1 ? adder_1_out : 4'bz;  // Controlled_Buffer controlled_buffer_2
  Subtractor #(.width(4)) subtractor_1 (
    .a(in_2), .b(in_3), .out(subtractor_1_out), .bout(subtractor_1_bout));  // open: bin
  assign SAIDA = decoder_1_out2 ? subtractor_1_out : 4'bz;  // Controlled_Buffer controlled_buffer_3
  nor nor_1 (ZERO, decoder_1_out7, decoder_1_out6, SAIDA[3], SAIDA[2], SAIDA[1], SAIDA[0]);
  assign or_2_out = in_3 | in_2;  // OR_Gate or_2, 4 bits wide
  assign SAIDA = decoder_1_out3 ? or_2_out : 4'bz;  // Controlled_Buffer controlled_buffer_4
  assign not_1_out = ~in_3;  // NOT_Gate not_1, 4 bits wide
  assign SAIDA = decoder_1_out4 ? not_1_out : 4'bz;  // Controlled_Buffer controlled_buffer_5
  Shifter #(.width(4), .shift("lr")) shifter_1 (.in(in_2), .\dist (in_3[1:0]), .out(shifter_1_out));
  Shifter #(.width(4)) shifter_2 (.in(in_2), .\dist (in_3[1:0]), .out(shifter_2_out));
  assign controlled_buffer_6_out = \DIREÇÃO  ? shifter_1_out : 4'bz;  // Controlled_Buffer controlled_buffer_6
  assign controlled_buffer_6_out = not_2_out ? shifter_2_out : 4'bz;  // Controlled_Buffer controlled_buffer_7
  not not_2 (not_2_out, \DIREÇÃO );
  assign SAIDA = decoder_1_out5 ? controlled_buffer_6_out : 4'bz;  // Controlled_Buffer controlled_buffer_8
endmodule

module main (
  input  [3:0] A,
  input  [3:0] B,
  input  \DIREÇÃO ,
  input  [2:0] \OPERAÇÃO ,
  output OVERFLOW,
  output ZERO,
  output [3:0] out_7
);

  ULA ula_1 (
    .\DIREÇÃO (\DIREÇÃO ), .in_2(A), .in_3(B), .ZERO(ZERO), .OVERFLOW(OVERFLOW), .in_4(\OPERAÇÃO ),
    .SAIDA(out_7));
endmodule

module Projeto_final (
  input  [3:0] in_1,
  input  Write___0____Read___1,
  input  \DIREÇAO ,
  output ZERO,
  output OVERFLOW
);

  wire clock_1_out, clock_2_out, clock_3_out, not_1_out, \unidade_de_controle_1_módulo_de_endereçamento ,
       ZERO_overflow, ZERO_zero;
  wire [2:0] unidade_de_controle_1_opcode;
  wire [3:0] multiplexer_1_out, ram_2_data, REGISTRADOR_AC_q, unidade_de_controle_1_operando, ZERO_saida;
  wire [7:0] ram_1_data, register_1_q;

  RAM #(.addrWidth(4)) ram_1 (.addr(in_1), .data(ram_1_data));  // open: sel, clk, ld, clr
  Clock clock_1 (.out(clock_1_out));
  Register register_1 (.D(ram_1_data), .Q(register_1_q), .clk(clock_1_out));  // open: en, clr
  UNIDADE_DE_CONTROLE unidade_de_controle_1 (
    .OPERANDO(unidade_de_controle_1_operando),
    .\MÓDULO_DE_ENDEREÇAMENTO (\unidade_de_controle_1_módulo_de_endereçamento ),
    .OPCODE(unidade_de_controle_1_opcode),
    .\INSTRUÇÃO___3___opcode___1___Mod_Endereçamento___4___Operando (register_1_q));
  Clock clock_2 (.out(clock_2_out));
  Clock clock_3 (.out(clock_3_out));
  // Probe on REGISTRADOR_AC_q
  Multiplexer #(.width(4)) multiplexer_1 (
    .in0(unidade_de_controle_1_operando), .in1(ram_2_data), .out(multiplexer_1_out),
    .sel(\unidade_de_controle_1_módulo_de_endereçamento ));  // open: en
  ULA u_ZERO (
    .\DIREÇÃO (\DIREÇAO ), .in_2(REGISTRADOR_AC_q), .in_3(multiplexer_1_out), .ZERO(ZERO_zero),
    .OVERFLOW(ZERO_overflow), .in_4(unidade_de_controle_1_opcode), .SAIDA(ZERO_saida));
  // Probe on ZERO_saida
  Register #(.width(4)) REGISTRADOR_AC (.D(ZERO_saida), .Q(REGISTRADOR_AC_q), .clk(clock_3_out));  // open: en, clr
  RAM #(.addrWidth(4), .dataWidth(4)) ram_2 (
    .addr(unidade_de_controle_1_operando), .data(ram_2_data), .clk(clock_2_out), .ld(Write___0____Read___1));  // open: sel, clr
  not not_1 (not_1_out, Write___0____Read___1);
  // Probe on multiplexer_1_out
  // Probe on ram_2_data
  assign ram_2_data = not_1_out ? REGISTRADOR_AC_q : 4'bz;  // Controlled_Buffer controlled_buffer_1
  Register #(.width(1)) REGISTRADOR_OVERFLOW (.D(ZERO_overflow), .Q(OVERFLOW), .clk(clock_3_out));  // open: en, clr
  Register #(.width(1)) REGISTRADOR_ZERO (.D(ZERO_zero), .Q(ZERO), .clk(clock_3_out));  // open: en, clr
endmodule

module UNIDADE_DE_CONTROLE (
  input  [7:0] \INSTRUÇÃO___3___opcode___1___Mod_Endereçamento___4___Operando ,
  output [3:0] OPERANDO,
  output \MÓDULO_DE_ENDEREÇAMENTO ,
  output [2:0] OPCODE
);


  assign \MÓDULO_DE_ENDEREÇAMENTO  = \INSTRUÇÃO___3___opcode___1___Mod_Endereçamento___4___Operando [4];
  assign OPCODE = \INSTRUÇÃO___3___opcode___1___Mod_Endereçamento___4___Operando [7:5];
  assign OPERANDO = \INSTRUÇÃO___3___opcode___1___Mod_Endereçamento___4___Operando [3:0];
endmodule
